# Fritzing sketch buttonsLEDs (saved by Fritzing 0.9.2b)
breadboards: 1

parts:
  J1 = T Cobbler Plus
  S1 = Momentary Switch [package=ksa_sealed_tac_switch]
  S2 = Momentary Switch [package=ksa_sealed_tac_switch]
  LED1 = smd LED [color="Yellow (595nm)" package="1206 [SMD]"]
  LED2 = smd LED [color="Red (635nm)" package="1206 [SMD]"]
  R1 = Resistor [tolerance=±5% resistance=330 package=THT]
  R2 = Resistor [tolerance=±5% resistance=330 package=THT]
  R4 = Resistor [tolerance=±5% resistance=10k package=THT]
  R5 = Resistor [tolerance=±5% resistance=10k package=THT]

nets:
  N1: J1.#23, S2.3, R4.Pin_1
  N2: J1.#24, S1.3, R5.Pin_1
  N3: J1.GND#38, LED1.anode
  N4: J1.#21, LED2.anode
  N5: S1.1, S2.1
  N6: LED1.cathode, R1.Pin_0
  N7: LED2.cathode, R2.Pin_0
  N8: R1.Pin_1, R2.Pin_1
  N9: R4.Pin_0, R5.Pin_0

custom parts:
  T Cobbler Plus: The T-Cobbler Plus is an add on prototyping board from Adafruit specifically designed for the Raspberry Pi B+ that can break out all those tasty power, GPIO, I2C and SPI pins from the 40-pin header onto a solderless breadboard. This set will make "cobbling together" prototypes with the Pi super easy. The T-Cobbler Plus can plug into any solderless breadboard.
